# Fritzing sketch pixels (saved by Fritzing 0.9.4)
circuit board: 8.46667cm x 5.64444cm
breadboards: 1

parts:
  Part1 = Arduino Pro Mini v13
  NEOPIXEL1 = Neopixel Strip -- Black (30/m) [part_number=1376]
  5V = 2.1mm Barrel Jack with Terminal Block
  1000_μF = Capacitor Polarized [package=cpol-radial-100uf-25v]
  Next_Animation = Pushbutton [package="[SMD]"]
  On/Off = Pushbutton [package="[SMD]"]
  R1 = Resistor [tolerance=±5% resistance=270 package="0402 [SMD]"]

nets:
  GND: Part1.GND, NEOPIXEL1.GND, 5V.NEG, 1000_μF.-, Next_Animation.Pin_1, Next_Animation.Pin_2, On/Off.Pin_3, On/Off.Pin_4
  VCC: Part1.VCC, NEOPIXEL1.+5V, 5V.POS, 1000_μF.+
  N1: Part1.D10_PWM/SS, R1.Pin_0
  N2: Part1.D3_PWM, On/Off.Pin_1, On/Off.Pin_2
  N3: Part1.D2, Next_Animation.Pin_3, Next_Animation.Pin_4
  N4: NEOPIXEL1.Din, R1.Pin_1

custom parts:
  Neopixel Strip -- Black (30/m): These NeoPixel strips have 30 digitally-addressable pixel LEDs per meter and are very affordable and are only 12.5 mm wide, 10 mm if you remove the strip from the casing.
